# Fritzing sketch schematic (saved by Fritzing 0.9.3b)

parts:
  WeMos_D1_Mini1 = WeMos D1 Mini
  Part1 = InvenSense MPU6050

nets:
  3V3: WeMos_D1_Mini1.3V3, Part1.VCC
  N1: WeMos_D1_Mini1.D1, Part1.SCL
  N2: WeMos_D1_Mini1.D2, Part1.SDA
  N3: WeMos_D1_Mini1.G, Part1.GND
